# Fritzing sketch simhubflaglights_sans_power (saved by Fritzing 0.9.9b)
circuit board: 8.46667cm x 5.64444cm
breadboards: 1

parts:
  Part1 = Arduino Nano (Rev3.0)
  R1 = Resistor [tolerance=±5% resistance=470 power=0.25 package="0603 [SMD]"]
  Part2 = NeoPixel NeoMatrix 8x8 [part_number=1487]
  C2 = Electrolytic Capacitor [capacitance=1000μF voltage=10V package="200 mil [THT, electrolytic]"]

nets:
  GND: Part1.GND, Part2.GND, C2.-
  N1: Part1.D6, R1.Pin_0
  5V: Part1.5V, Part2.VDD, C2.+
  N2: R1.Pin_1, Part2.IN

custom parts:
  NeoPixel NeoMatrix 8x8: Put on your sunglasses before wiring up this LED matrix - 64 eye-blistering RGB LEDs adorn the NeoMatrix for a blast of configurable color. Arranged in an 8x8 matrix, each pixel is individually addressable. Only one microcontroller pin is required to control all the LEDs, and you get 24 bit color for each LED.
